# Fritzing sketch minibot_arduino (saved by Fritzing 0.9.10b)

parts:
  Part1 = Arduino Mega 2560 (Rev3)
  Arduino_MEGA_Shield = Arduino Mega Sensor Shield v2.0
  L298N1 = L298N DC motor driver
  LEFT_MOTOR = DC Motor with two-phase hall-encoder [part_number=VT-E-G25A-06-177E]
  RIGHT_MOTOR = DC Motor with two-phase hall-encoder [part_number=VT-E-G25A-06-177E]
  Raspberry_Pi_4B = Raspberry Pi 4B  # not connected
  12V-5V_DC-DC_Converter = RioRand LM2596
  18650_Batteries_(3_7x3=11_1V) = 18650 battery holder [package=battery-18650-kit]
  BAT2 = 18650 battery holder [package=battery-18650-kit]
  BAT3 = 18650 battery holder [package=battery-18650-kit]

nets:
  N1: Part1.A8, Arduino_MEGA_Shield.pin_8, Arduino_MEGA_Shield.pin_252
  N2: Part1.A9, Arduino_MEGA_Shield.pin_9, Arduino_MEGA_Shield.pin_255
  N3: Part1.A10, Arduino_MEGA_Shield.pin_10, Arduino_MEGA_Shield.pin_258
  N4: Part1.A11, Arduino_MEGA_Shield.pin_11, Arduino_MEGA_Shield.pin_261
  N5: Part1.A12, Arduino_MEGA_Shield.pin_12, Arduino_MEGA_Shield.pin_288
  N6: Part1.A13, Arduino_MEGA_Shield.pin_13, Arduino_MEGA_Shield.pin_291
  N7: Part1.A14, Arduino_MEGA_Shield.pin_14, Arduino_MEGA_Shield.pin_294
  N8: Part1.A15, Arduino_MEGA_Shield.pin_15, Arduino_MEGA_Shield.pin_297
  N9: Part1.A0, Arduino_MEGA_Shield.pin0, Arduino_MEGA_Shield.pin_180
  N10: Part1.A1, Arduino_MEGA_Shield.pin_1, Arduino_MEGA_Shield.pin_183
  N11: Part1.A2, Arduino_MEGA_Shield.pin_2, Arduino_MEGA_Shield.pin_186
  N12: Part1.A3, Arduino_MEGA_Shield.pin_3, Arduino_MEGA_Shield.pin_189
  N13: Part1.A4, Arduino_MEGA_Shield.pin_4, Arduino_MEGA_Shield.pin_216
  N14: Part1.A5, Arduino_MEGA_Shield.pin_5, Arduino_MEGA_Shield.pin_219
  N15: Part1.A6, Arduino_MEGA_Shield.pin_6, Arduino_MEGA_Shield.pin_222
  N16: Part1.A7, Arduino_MEGA_Shield.pin_7, Arduino_MEGA_Shield.pin_225
  N17: Part1.D21/SCL, Arduino_MEGA_Shield.pin_38, Arduino_MEGA_Shield.pin_273, RIGHT_MOTOR.pin5
  N18: Part1.D20/SDA, Part1.SDA, Arduino_MEGA_Shield.pin_39
  N19: Part1.D19/RX1, Arduino_MEGA_Shield.pin_40, Arduino_MEGA_Shield.pin_267, LEFT_MOTOR.pin5
  N20: Part1.D18/TX1, Arduino_MEGA_Shield.pin_41
  N21: Part1.D17_PWM/RX2, Arduino_MEGA_Shield.pin_42, Arduino_MEGA_Shield.pin_237
  N22: Part1.D16_PWM/TX2, Arduino_MEGA_Shield.pin_43, Arduino_MEGA_Shield.pin_234
  N23: Part1.D15/RX3, Arduino_MEGA_Shield.pin_44, Arduino_MEGA_Shield.pin_231
  N24: Part1.D14/TX3, Arduino_MEGA_Shield.pin_45, Arduino_MEGA_Shield.pin_228
  N25: Part1.AREF, Arduino_MEGA_Shield.pin_37, Arduino_MEGA_Shield.pin_84
  N26: Part1.GND, Arduino_MEGA_Shield.pin_19, Arduino_MEGA_Shield.pin_20, Arduino_MEGA_Shield.pin_36, Arduino_MEGA_Shield.pin_80, Arduino_MEGA_Shield.pin_81, Arduino_MEGA_Shield.pin_229, Arduino_MEGA_Shield.pin_262, Arduino_MEGA_Shield.pin_265, Arduino_MEGA_Shield.pin_268, Arduino_MEGA_Shield.pin_271, Arduino_MEGA_Shield.pin_326, LEFT_MOTOR.pin3, LEFT_MOTOR.pin4, RIGHT_MOTOR.pin3, RIGHT_MOTOR.pin4
  N27: Part1.D13_PWM, Arduino_MEGA_Shield.pin_35, Arduino_MEGA_Shield.pin_90
  N28: Part1.D12_PWM, Arduino_MEGA_Shield.pin_34, Arduino_MEGA_Shield.pin_93, L298N1.IN4
  N29: Part1.D11_PWM, Arduino_MEGA_Shield.pin_33, Arduino_MEGA_Shield.pin_120, L298N1.IN3
  N30: Part1.D10_PWM, Arduino_MEGA_Shield.pin_32, Arduino_MEGA_Shield.pin_123, L298N1.IN2
  N31: Part1.D9_PWM, Arduino_MEGA_Shield.pin_31, Arduino_MEGA_Shield.pin_126, L298N1.IN1
  N32: Part1.D8_PWM, Arduino_MEGA_Shield.pin_30, Arduino_MEGA_Shield.pin_129
  N33: Part1.RESET, Arduino_MEGA_Shield.pin_16, Arduino_MEGA_Shield.pin_298
  N34: Part1.3V3, Arduino_MEGA_Shield.pin_17, Arduino_MEGA_Shield.pin_308
  N35: Part1.5V, Arduino_MEGA_Shield.pin_18, Arduino_MEGA_Shield.pin_46, Arduino_MEGA_Shield.pin_47, Arduino_MEGA_Shield.pin_303
  N36: Part1.VIN, Arduino_MEGA_Shield.pin_21
  N37: Part1.D0_RX0, Arduino_MEGA_Shield.pin_22, Arduino_MEGA_Shield.pin_310
  N38: Part1.D1_TX0, Arduino_MEGA_Shield.pin_23, Arduino_MEGA_Shield.pin_311
  N39: Part1.D2_PWM, Arduino_MEGA_Shield.pin_24, Arduino_MEGA_Shield.pin_195
  N40: Part1.D3_PWM, Arduino_MEGA_Shield.pin_25, Arduino_MEGA_Shield.pin_192
  N41: Part1.D4_PWM, Arduino_MEGA_Shield.pin_26, Arduino_MEGA_Shield.pin_165
  N42: Part1.D5_PWM, Arduino_MEGA_Shield.pin_27, Arduino_MEGA_Shield.pin_162
  N43: Part1.D6_PWM, Arduino_MEGA_Shield.pin_28, Arduino_MEGA_Shield.pin_159
  N44: Part1.D7_PWM, Arduino_MEGA_Shield.pin_29, Arduino_MEGA_Shield.pin_156
  N45: Part1.D22, Arduino_MEGA_Shield.pin_48, Arduino_MEGA_Shield.pin_96
  N46: Part1.D23, Arduino_MEGA_Shield.pin_49, Arduino_MEGA_Shield.pin_99
  N47: Part1.D24, Arduino_MEGA_Shield.pin_50, Arduino_MEGA_Shield.pin_102
  N48: Part1.D25, Arduino_MEGA_Shield.pin_51, Arduino_MEGA_Shield.pin_105
  N49: Part1.D26, Arduino_MEGA_Shield.pin_52, Arduino_MEGA_Shield.pin_132
  N50: Part1.D27, Arduino_MEGA_Shield.pin_53, Arduino_MEGA_Shield.pin_135
  N51: Part1.D28, Arduino_MEGA_Shield.pin_54, Arduino_MEGA_Shield.pin_138
  N52: Part1.D29, Arduino_MEGA_Shield.pin_55, Arduino_MEGA_Shield.pin_141
  N53: Part1.D30, Arduino_MEGA_Shield.pin_56, Arduino_MEGA_Shield.pin_168
  N54: Part1.D31, Arduino_MEGA_Shield.pin_57, Arduino_MEGA_Shield.pin_171
  N55: Part1.D32, Arduino_MEGA_Shield.pin_58, Arduino_MEGA_Shield.pin_174
  N56: Part1.D33, Arduino_MEGA_Shield.pin_59, Arduino_MEGA_Shield.pin_177
  N57: Part1.D34, Arduino_MEGA_Shield.pin_60, Arduino_MEGA_Shield.pin_204
  N58: Part1.D35, Arduino_MEGA_Shield.pin_61, Arduino_MEGA_Shield.pin_207
  N59: Part1.D36, Arduino_MEGA_Shield.pin_62, Arduino_MEGA_Shield.pin_210
  N60: Part1.D37, Arduino_MEGA_Shield.pin_63, Arduino_MEGA_Shield.pin_213
  N61: Part1.D38, Arduino_MEGA_Shield.pin_64, Arduino_MEGA_Shield.pin_240
  N62: Part1.D39, Arduino_MEGA_Shield.pin_65, Arduino_MEGA_Shield.pin_243
  N63: Part1.D40, Arduino_MEGA_Shield.pin_66, Arduino_MEGA_Shield.pin_246
  N64: Part1.D41, Arduino_MEGA_Shield.pin_67, Arduino_MEGA_Shield.pin_249
  N65: Part1.D42, Arduino_MEGA_Shield.pin_68, Arduino_MEGA_Shield.pin_276
  N66: Part1.D43, Arduino_MEGA_Shield.pin_69, Arduino_MEGA_Shield.pin_279
  N67: Part1.D44, Arduino_MEGA_Shield.pin_70, Arduino_MEGA_Shield.pin_282
  N68: Part1.D45, Arduino_MEGA_Shield.pin_71, Arduino_MEGA_Shield.pin_285
  N69: Part1.D46, Arduino_MEGA_Shield.pin_72, Arduino_MEGA_Shield.pin_108
  N70: Part1.D47, Arduino_MEGA_Shield.pin_73, Arduino_MEGA_Shield.pin_111
  N71: Part1.D48, Arduino_MEGA_Shield.pin_74, Arduino_MEGA_Shield.pin_114
  N72: Part1.D49, Arduino_MEGA_Shield.pin_75, Arduino_MEGA_Shield.pin_117
  N73: Part1.D50, Arduino_MEGA_Shield.pin_76, Arduino_MEGA_Shield.pin_314
  N74: Part1.D51, Arduino_MEGA_Shield.pin_77, Arduino_MEGA_Shield.pin_317
  N75: Part1.D52, Arduino_MEGA_Shield.pin_78, Arduino_MEGA_Shield.pin_315
  N76: Part1.D53, Arduino_MEGA_Shield.pin_79, Arduino_MEGA_Shield.pin_316
  N77: Arduino_MEGA_Shield.pin_227, Arduino_MEGA_Shield.pin_266, Arduino_MEGA_Shield.pin_272, LEFT_MOTOR.pin2, RIGHT_MOTOR.pin2
  N78: L298N1.OUT1, LEFT_MOTOR.pin1
  N79: L298N1.OUT2, LEFT_MOTOR.pin6
  N80: L298N1.OUT3, RIGHT_MOTOR.pin1
  N81: L298N1.OUT4, RIGHT_MOTOR.pin6
  N82: L298N1.5V#9, L298N1.ENA
  N83: L298N1.5V#10, L298N1.ENB
  N84: 12V-5V_DC-DC_Converter.Pin_1, 18650_Batteries_(3_7x3=11_1V).-
  N85: 12V-5V_DC-DC_Converter.Pin_2, BAT3.+
  N86: 18650_Batteries_(3_7x3=11_1V).+, BAT2.-
  N87: BAT2.+, BAT3.-

custom parts:
  L298N DC motor driver: 2x DC motor driver with 78M05 positive voltage regulator (7..35 V) L298N: max 46 V, 2 A Set 5 V Enable jumper to enable 5 V regultor (needed for the L298N) and +5 V output at screw terminal or supply external +5 V at screw terminal Set ENA and/or ENB to +5 V to enable motor permanently or supply ENA and/or ENB with PWM signal IN1 and IN2 set rotation directory for motor A (OUT1/OUT2) IN2 and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
  18650 battery holder: 18650 Battery Holder identical to the dual battery version.
