# Fritzing sketch xl4016Sketch (saved by Fritzing 0.9.3b)

parts:
  DC1 = DC_DC_XL4016 [chip_label=XL4016 package=board_screw]
  J1 = female pin header, 1 pin [form="♀ (female)"]
  J2 = female pin header, 1 pin [form="♀ (female)"]
  J3 = female pin header, 1 pin [form="♀ (female)"]
  J4 = female pin header, 1 pin [form="♀ (female)"]

nets:
  N1: DC1.IN+, J4.pin1
  N2: DC1.IN-, J3.pin1
  N3: DC1.OUT+, J1.pin1
  N4: DC1.OUT-, J2.pin1

custom parts:
  DC_DC_XL4016: DC-DC Converter step down voltage regulator XL4016 custom sketch.
